// Logisim project resurse_proiect.circ as structural Verilog
module main (
  input  in_1,
  input  in_2,
  output out_3
);

  counter_10min counter_10min_1 (.CLK_1MIN(in_1), .EN10(in_2), .T10(out_3));
endmodule

module proiectv3 (
  input  CLOSE_OPEN_DOOR,
  input  START,
  input  RESET,
  input  MANUAL_MODE,
  input  CLK,
  input  SET_TEMPERATURE,
  input  SET_SPEED,
  input  SET_PREWASH,
  input  SET_ADD_RINSE,
  input  FAST_WASH,
  input  SHIRTS,
  input  DARK_CLOTHES,
  input  DIRTY_LAUNDRY,
  input  ANTIALLERGEN,
  output DOOR_CLOSED,
  output [3:0] ANOD,
  output DOOR_BLOCKED,
  output [6:0] CATOD,
  output PREWASH,
  output MAIN_WASH,
  output RINSE,
  output ADDITIONAL_RINSE,
  output CENTRIFUGE,
  output [3:0] TEMPERATURE,
  output [2:0] SPEED,
  output PREWASH_OPTION,
  output ADDITIONAL_RINSE_OPTION
);

  wire check_can_start_1_can_start, counter_1min_1_t1, counter_10min_1_t10, counter_20min_1_t20,
       counter_delay_1_y, debouncer_30ns_1_btn_dis, debouncer_30ns_2_btn_dis, debouncer_30ns_3_btn_dis,
       debouncer_30ns_4_btn_dis, debouncer_30ns_5_btn_dis, divizor_frecventa_1min_1_clk_1min,
       divizor_frecventa_1min_2_clk_1min, divizor_frecventa_2sec_1_clk_2sec,
       divizor_frecventa_2sec_2_clk_2sec, divizor_frecventa_200hz_1_clk_out, heater_1_temperature,
       memorie_rom_1_program_additional_rinse, memorie_rom_1_program_prewash, uc_1_en1, uc_1_en10, uc_1_en20,
       uc_1_en_1min, uc_1_en_2sec, uc_1_en_time, uc_1_en_water, uc_1_load_delay, uc_1_load_time_left,
       uc_1_mesaj, uc_1_start_program;
  wire [1:0] uc_1_mode;
  wire [2:0] encoder_stan_1_encoded, memorie_rom_1_program_speed;
  wire [3:0] memorie_rom_1_program_temperature;
  wire [5:0] calculate_total_time_1_delay;
  wire [6:0] calculate_temperature_1_temperature, calculate_total_time_1_total_time,
       counter_time_left_1_time_left, mux_2_1_7bits_1_time_for_ssd;

  debouncer_30ns debouncer_30ns_1 (.BTN(START), .CLK_100MHZ(CLK), .BTN_DIS(debouncer_30ns_1_btn_dis));
  divizor_frecventa_200Hz divizor_frecventa_200hz_1 (.clk_in(CLK), .clk_out(divizor_frecventa_200hz_1_clk_out));
  Encoder encoder_stan_1 (
    .A0(FAST_WASH), .A1(SHIRTS), .A2(DARK_CLOTHES), .A3(DIRTY_LAUNDRY), .A4(ANTIALLERGEN),
    .ENCODED(encoder_stan_1_encoded));
  divizor_frecventa_2sec divizor_frecventa_2sec_2 (
    .EN(uc_1_en_2sec), .CLK(CLK), .CLK_2SEC(divizor_frecventa_2sec_2_clk_2sec));
  debouncer_30ns debouncer_30ns_2 (.BTN(SET_TEMPERATURE), .CLK_100MHZ(CLK), .BTN_DIS(debouncer_30ns_2_btn_dis));
  debouncer_30ns debouncer_30ns_3 (.BTN(SET_SPEED), .CLK_100MHZ(CLK), .BTN_DIS(debouncer_30ns_3_btn_dis));
  debouncer_30ns debouncer_30ns_4 (.BTN(SET_PREWASH), .CLK_100MHZ(CLK), .BTN_DIS(debouncer_30ns_4_btn_dis));
  debouncer_30ns debouncer_30ns_5 (.BTN(SET_ADD_RINSE), .CLK_100MHZ(CLK), .BTN_DIS(debouncer_30ns_5_btn_dis));
  MEMORIE_ROM memorie_rom_1 (
    .PROGRAM_SELECTED(encoder_stan_1_encoded), .PROGRAM_TEMPERATURE(memorie_rom_1_program_temperature),
    .PROGRAM_SPEED(memorie_rom_1_program_speed), .PROGRAM_PREWASH(memorie_rom_1_program_prewash),
    .PROGRAM_ADDITIONAL_RINSE(memorie_rom_1_program_additional_rinse));
  UC uc_1 (
    .CLOSE_OPEN_DOOR(CLOSE_OPEN_DOOR), .START(debouncer_30ns_1_btn_dis), .RESET(RESET), .CLK(CLK),
    .MANUAL_MODE(MANUAL_MODE), .T20(counter_20min_1_t20), .T10(counter_10min_1_t10), .T1(counter_1min_1_t1),
    .CAN_START(check_can_start_1_can_start), .TEMPERATURE_REACHED(heater_1_temperature),
    .PREWASH(PREWASH_OPTION), .ADDITIONAL_RINSE(ADDITIONAL_RINSE_OPTION), .DOOR_CLOSED(DOOR_CLOSED),
    .DOOR_BLOCKED(DOOR_BLOCKED), .STAGE1(PREWASH), .STAGE2(MAIN_WASH), .STAGE3(RINSE),
    .STAGE4(ADDITIONAL_RINSE), .STAGE5(CENTRIFUGE), .EN20(uc_1_en20), .EN10(uc_1_en10), .EN1(uc_1_en1),
    .EN_WATER(uc_1_en_water), .START_PROGRAM(uc_1_start_program), .EN_TIME(uc_1_en_time),
    .EN_2SEC(uc_1_en_2sec), .EN_1MIN(uc_1_en_1min), .MODE(uc_1_mode), .MESAJ(uc_1_mesaj),
    .LOAD_TIME_LEFT(uc_1_load_time_left), .LOAD_DELAY(uc_1_load_delay));
  divizor_frecventa_1min divizor_frecventa_1min_2 (
    .EN(uc_1_en_1min), .CLK_2SEC(divizor_frecventa_2sec_2_clk_2sec),
    .CLK_1MIN(divizor_frecventa_1min_2_clk_1min));
  registru_4biti registru_4biti_1 (
    .MODE(uc_1_mode), .PL(memorie_rom_1_program_temperature), .BTN(debouncer_30ns_2_btn_dis), .CLK(CLK),
    .Y(TEMPERATURE));
  registru_3biti registru_3biti_1 (
    .MODE(uc_1_mode), .PL(memorie_rom_1_program_speed), .BTN(debouncer_30ns_3_btn_dis), .CLK(CLK), .Y(SPEED));
  registru_1bit registru_1bit_1 (
    .MODE(uc_1_mode), .PL(memorie_rom_1_program_prewash), .BTN(debouncer_30ns_4_btn_dis), .CLK(CLK),
    .Y(PREWASH_OPTION));
  registru_1bit registru_1bit_2 (
    .MODE(uc_1_mode), .PL(memorie_rom_1_program_additional_rinse), .BTN(debouncer_30ns_5_btn_dis), .CLK(CLK),
    .Y(ADDITIONAL_RINSE_OPTION));
  counter_20min counter_20min_1 (
    .CLK_1MIN(divizor_frecventa_1min_2_clk_1min), .EN20(uc_1_en20), .T20(counter_20min_1_t20));
  counter_10min counter_10min_1 (
    .CLK_1MIN(divizor_frecventa_1min_2_clk_1min), .EN10(uc_1_en10), .T10(counter_10min_1_t10));
  counter_1min counter_1min_1 (
    .CLK_1MIN(divizor_frecventa_1min_2_clk_1min), .EN_1MIN(uc_1_en1), .T1(counter_1min_1_t1));
  Heater heater_1 (
    .EN_WATER(uc_1_en_water), .CLK_2SEC(divizor_frecventa_2sec_2_clk_2sec),
    .TEMP(calculate_temperature_1_temperature), .TEMPERATURE(heater_1_temperature));
  divizor_frecventa_2sec divizor_frecventa_2sec_1 (
    .EN(uc_1_en_time), .CLK(CLK), .CLK_2SEC(divizor_frecventa_2sec_1_clk_2sec));
  calculate_total_time calculate_total_time_1 (
    .PREWASH(PREWASH_OPTION), .ADDITIONAL_RINSE(ADDITIONAL_RINSE_OPTION), .TEMPERATURE(TEMPERATURE),
    .TOTAL_TIME(calculate_total_time_1_total_time), .DELAY(calculate_total_time_1_delay));
  counter_delay counter_delay_1 (
    .EN(uc_1_en_time), .CLK_2SEC(divizor_frecventa_2sec_1_clk_2sec), .DELAY(calculate_total_time_1_delay),
    .LOAD_DELAY(uc_1_load_delay), .Y(counter_delay_1_y));
  calculate_temperature calculate_temperature_1 (
    .temp_mode(TEMPERATURE), .TEMPERATURE(calculate_temperature_1_temperature));
  check_can_start check_can_start_1 (.TEMPERATURE(TEMPERATURE), .SPEED(SPEED), .CAN_START(check_can_start_1_can_start));
  SSD_PROIECT ssd_proiect_1 (
    .Mesaj(uc_1_mesaj), .\input (mux_2_1_7bits_1_time_for_ssd), .CLK(divizor_frecventa_200hz_1_clk_out),
    .anod(ANOD), .catod(CATOD));
  divizor_frecventa_1min divizor_frecventa_1min_1 (
    .EN(counter_delay_1_y), .CLK_2SEC(divizor_frecventa_2sec_1_clk_2sec),
    .CLK_1MIN(divizor_frecventa_1min_1_clk_1min));
  counter_time_left counter_time_left_1 (
    .TOTAL_TIME(calculate_total_time_1_total_time), .CLK_1MIN(divizor_frecventa_1min_1_clk_1min),
    .EN_TIME(counter_delay_1_y), .LOAD(uc_1_load_time_left), .TIME_LEFT(counter_time_left_1_time_left));
  MUX_2_1_7BITS mux_2_1_7bits_1 (
    .TOTAL_TIME(calculate_total_time_1_total_time), .TIME_LEFT(counter_time_left_1_time_left),
    .START_PROGRAM(uc_1_start_program), .TIME_FOR_SSD(mux_2_1_7bits_1_time_for_ssd));
endmodule

// VHDL entity divizor_frecventa_2sec, as the project stores it:
--STAN MIHAI ALEXANDRU
LIBRARY ieee;
USE ieee.std_logic_1164.all;

USE ieee.std_logic_unsigned.all;
ENTITY divizor_frecventa_2sec IS
  PORT (
  	EN, CLK: IN STD_LOGIC;
  	CLK_2SEC: OUT STD_LOGIC
    );
END divizor_frecventa_2sec;

--------------------------------------------------------------------------------
--Complete your VHDL description below
--------------------------------------------------------------------------------

ARCHITECTURE TypeArchitecture OF divizor_frecventa_2sec IS

SIGNAL AUX: STD_LOGIC := '0';

BEGIN

CLK_2SEC <= AUX;

PROCESS(EN, CLK)
VARIABLE NR: INTEGER := 0;
BEGIN
	IF EN = '0' THEN
		AUX <= '0';
		NR := 0;
	ELSE
		IF RISING_EDGE(CLK) THEN
			NR := NR + 1;
			--IF NR = 100_000_000 THEN
			IF NR = 1_000_000 THEN
				AUX <= NOT AUX;
				NR := 0;
			ELSE
				NULL;
			END IF;
		END IF;
	END IF;
END PROCESS;

END TypeArchitecture;

// VHDL entity divizor_frecventa_1min, as the project stores it:
-- STAN MIHAI ALEXANDRU
LIBRARY ieee;
USE ieee.std_logic_1164.all;

ENTITY divizor_frecventa_1min IS
  PORT (
  	EN, CLK_2SEC: IN STD_LOGIC;
  	CLK_1MIN: OUT STD_LOGIC
    );
END divizor_frecventa_1min;

ARCHITECTURE TypeArchitecture OF divizor_frecventa_1min IS
SIGNAL AUX: STD_LOGIC := '0';

BEGIN

CLK_1MIN <= AUX;

PROCESS(EN, CLK_2SEC)
VARIABLE NR: INTEGER := 0;
BEGIN
	IF EN = '0' THEN
		AUX <= '0';
		NR := 0;
	ELSE
		IF FALLING_EDGE(CLK_2SEC) THEN
			NR := NR + 1;
			IF NR = 15 THEN
				AUX <= NOT AUX;
				NR := 0;
			ELSE
				NULL;
			END IF;
		END IF;
	END IF;
END PROCESS;

END TypeArchitecture;

// VHDL entity registru_4biti, as the project stores it:
--TOSA CEZAR
LIBRARY ieee;
USE ieee.std_logic_1164.all;

ENTITY registru_4biti IS
  PORT (
	MODE: IN STD_LOGIC_VECTOR(1 DOWNTO 0);
	PL: IN STD_LOGIC_VECTOR(3 DOWNTO 0);
	BTN, CLK: IN STD_LOGIC;
	Y: OUT STD_LOGIC_VECTOR(3 DOWNTO 0)
    );
END registru_4biti;


ARCHITECTURE TypeArchitecture OF registru_4biti IS

SIGNAL Y_TEMP: STD_LOGIC_VECTOR(3 DOWNTO 0) := "0000";

BEGIN

PROCESS(CLK)
VARIABLE WAS_ON: STD_LOGIC := '0';
BEGIN
	IF RISING_EDGE(CLK) THEN
		CASE MODE IS
			WHEN "00" => 
				IF BTN = '1' THEN
					WAS_ON := '1';
				ELSE
					NULL;
				END IF;
			WHEN "01" => 
				Y_TEMP <= PL;
				WAS_ON := '0';
			WHEN "10" => 
				IF BTN = '0' AND WAS_ON = '1' THEN
					IF Y_TEMP = "0000" THEN
						Y_TEMP <= "1000";
					ELSE
						Y_TEMP <= Y_TEMP(0) & Y_TEMP(3 DOWNTO 1);
					END IF;
					WAS_ON :='0';
				ELSE NULL;
				END IF;
				IF BTN = '1' THEN
					WAS_ON := '1';
				ELSE
					NULL;
				END IF;
			WHEN "11" => Y_TEMP <= "0000";
			WHEN OTHERS => NULL;
		END CASE;
	END IF;
END PROCESS;

Y <= Y_TEMP;

END TypeArchitecture;

// VHDL entity registru_3biti, as the project stores it:
--TOSA CEZAR
LIBRARY ieee;
USE ieee.std_logic_1164.all;

ENTITY registru_3biti IS
  PORT (
	MODE: IN STD_LOGIC_VECTOR(1 DOWNTO 0);
	PL: IN STD_LOGIC_VECTOR(2 DOWNTO 0);
	BTN, CLK: IN STD_LOGIC;
	Y: OUT STD_LOGIC_VECTOR(2 DOWNTO 0)
    );
END registru_3biti;


ARCHITECTURE TypeArchitecture OF registru_3biti IS

SIGNAL Y_TEMP: STD_LOGIC_VECTOR(2 DOWNTO 0) := "000";

BEGIN

PROCESS(CLK)
VARIABLE WAS_ON: STD_LOGIC := '0';
BEGIN
	IF RISING_EDGE(CLK) THEN
		CASE MODE IS
			WHEN "00" => 
				IF BTN = '1' THEN
					WAS_ON := '1';
				ELSE
					NULL;
				END IF;
			WHEN "01" => 
				Y_TEMP <= PL;
				WAS_ON := '0';
			WHEN "10" => 
				IF BTN = '0' AND WAS_ON = '1' THEN
					IF Y_TEMP = "000" THEN
						Y_TEMP <= "100";
					ELSE
						Y_TEMP <= Y_TEMP(0) & Y_TEMP(2 DOWNTO 1);
					END IF;
					WAS_ON :='0';
				ELSE NULL;
				END IF;
				IF BTN = '1' THEN
					WAS_ON := '1';
				ELSE
					NULL;
				END IF;
			WHEN "11" => Y_TEMP <= "000";
			WHEN OTHERS => NULL;
		END CASE;
	END IF;
END PROCESS;

Y <= Y_TEMP;

END TypeArchitecture;

// VHDL entity UC, as the project stores it:
--TOSA CEZAR
LIBRARY ieee;
USE ieee.std_logic_1164.all;

ENTITY UC IS
  PORT (
	  CLOSE_OPEN_DOOR: IN STD_LOGIC;
	  START: IN STD_LOGIC;
	  RESET: IN STD_LOGIC;
	  CLK: IN STD_LOGIC;
	  MANUAL_MODE: IN STD_LOGIC;
	  T20, T10, T1: IN STD_LOGIC;
	  CAN_START: IN STD_LOGIC;
	  TEMPERATURE_REACHED: IN STD_LOGIC;
	  PREWASH, ADDITIONAL_RINSE: IN STD_LOGIC;
	  DOOR_CLOSED: OUT STD_LOGIC;
	  DOOR_BLOCKED: OUT STD_LOGIC;
	  STAGE1, STAGE2, STAGE3, STAGE4, STAGE5: OUT STD_LOGIC;
	  EN20, EN10, EN1: OUT STD_LOGIC;
	  EN_WATER: OUT STD_LOGIC;
	  START_PROGRAM: OUT STD_LOGIC;
	  EN_TIME: OUT STD_LOGIC;
	  EN_2SEC, EN_1MIN: OUT STD_LOGIC;
	  MODE: OUT STD_LOGIC_VECTOR(1 DOWNTO 0);
	  MESAJ: OUT STD_LOGIC;
	  LOAD_TIME_LEFT: OUT STD_LOGIC;
	  LOAD_DELAY: OUT STD_LOGIC
    );
END UC;

--------------------------------------------------------------------------------
--Complete your VHDL description below
--------------------------------------------------------------------------------

ARCHITECTURE TypeArchitecture OF UC IS

TYPE STATE_T IS (INITIAL_STATE, WAITING, N1, N2, N3, N4, N5, N6, N7, N8, N9, N10, 
			N11, N12, N13, C1, C2, C3, C4, C5, C6, C7, C8, C9);
SIGNAL STATE, NXT_STATE: STATE_T := INITIAL_STATE;

BEGIN

-- SETAM URMATOAREA STARE
PROCESS(CLK, RESET)
BEGIN
	IF RESET = '1' THEN STATE <= INITIAL_STATE;
	ELSE
		IF RISING_EDGE(CLK) THEN
			STATE <= NXT_STATE;
		END IF;
	END IF;
END PROCESS;


-- STABILIM IESIRILE IN FUNCTIE DE FIECARE STARE
PROCESS(STATE)
BEGIN
	DOOR_CLOSED <= '0';
	DOOR_BLOCKED <= '0';
	STAGE1 <= '0';
	STAGE2 <= '0';
	STAGE3 <= '0';
	STAGE4 <= '0';
	STAGE5 <= '0';
	EN10 <= '0';
	EN20 <= '0';
	EN1 <= '0';
	EN_WATER <= '0';
	START_PROGRAM <= '0';
	EN_TIME <= '0';
	EN_2SEC <= '0';
	EN_1MIN <= '0';
	MODE <= "00";
	MESAJ <= '0';
	LOAD_TIME_LEFT <= '0';
	LOAD_DELAY <= '0';

	CASE STATE IS
		WHEN INITIAL_STATE =>
			MODE <= "11";
			
		WHEN WAITING => 
			NULL;
			
		WHEN N1 =>
			MODE <= "10";
			
		WHEN N2 => 
			MODE <= "01";
			
		WHEN N3 => 
			NULL;
			
		WHEN N4 =>
			DOOR_CLOSED <= '1';

		WHEN N5 =>
			DOOR_CLOSED <= '1';
			DOOR_BLOCKED <= '1';
			LOAD_DELAY <= '1';
			LOAD_TIME_LEFT <= '1';
			
		WHEN N6 =>
			DOOR_CLOSED <= '1';
			START_PROGRAM <= '1';
			DOOR_BLOCKED <= '1';
			EN_TIME <= '1';		
			
		WHEN C1 =>
			DOOR_CLOSED <= '1';
			START_PROGRAM <= '1';
			DOOR_BLOCKED <= '1';
			EN_TIME <= '1';
			EN_WATER <= '1';
			STAGE1 <= '1';
			EN_2SEC <= '1';
			
		WHEN C2 =>
			DOOR_CLOSED <= '1';
			START_PROGRAM <= '1';
			DOOR_BLOCKED <= '1';
			EN_TIME <= '1';
			STAGE1 <= '1';
			
		WHEN C3 =>
			DOOR_CLOSED <= '1';
			START_PROGRAM <= '1';
			DOOR_BLOCKED <= '1';
			EN_TIME <= '1';
			EN_2SEC <= '1';
			EN_1MIN <= '1';
			EN10  <= '1';
			STAGE1 <= '1';
			
		WHEN N7 =>
			DOOR_CLOSED <= '1';
			START_PROGRAM <= '1';
			DOOR_BLOCKED <= '1';
			EN_TIME <= '1';
			
		WHEN C4 =>
			DOOR_CLOSED <= '1';
			START_PROGRAM <= '1';
			DOOR_BLOCKED <= '1';
			EN_TIME <= '1';
			EN_WATER <= '1';
			EN_2SEC <= '1';
			STAGE2 <= '1';
			
		WHEN C5 =>
			DOOR_CLOSED <= '1';
			START_PROGRAM <= '1';
			DOOR_BLOCKED <= '1';
			EN_TIME <= '1';
			STAGE2 <= '1';
			
		WHEN C6 =>
			DOOR_CLOSED <= '1';
			START_PROGRAM <= '1';
			DOOR_BLOCKED <= '1';
			EN_TIME <= '1';
			EN20 <= '1';
			EN_2SEC <= '1';
			EN_1MIN <= '1';
			STAGE2 <= '1';
			
		WHEN N8 =>
			DOOR_CLOSED <= '1';
			START_PROGRAM <= '1';
			DOOR_BLOCKED <= '1';
			EN_TIME <= '1';
			
		WHEN C7 =>
			DOOR_CLOSED <= '1';
			START_PROGRAM <= '1';
			DOOR_BLOCKED <= '1';
			EN_TIME <= '1';
			EN_2SEC <= '1';
			EN_1MIN <= '1';
			EN10 <= '1';
			STAGE3 <= '1';
			
		WHEN N9 =>
			DOOR_CLOSED <= '1';
			START_PROGRAM <= '1';
			DOOR_BLOCKED <= '1';
			EN_TIME <= '1';
			
		WHEN C8 =>
			DOOR_CLOSED <= '1';
			START_PROGRAM <= '1';
			DOOR_BLOCKED <= '1';
			EN_TIME <= '1';
			EN_2SEC <= '1';
			EN_1MIN <= '1';
			EN10 <= '1';
			STAGE4 <= '1';

		WHEN N10 =>
			DOOR_CLOSED <= '1';
			START_PROGRAM <= '1';
			DOOR_BLOCKED <= '1';
			EN_TIME <= '1';
			
		WHEN C9 =>
			DOOR_CLOSED <= '1';
			START_PROGRAM <= '1';
			DOOR_BLOCKED <= '1';
			EN_TIME <= '1';
			EN_2SEC <= '1';
			EN_1MIN <= '1';
			EN10 <= '1';
			STAGE5 <= '1';
			
		WHEN N11 =>
			DOOR_CLOSED <= '1';
			START_PROGRAM <= '1';
			DOOR_BLOCKED <= '1';
			EN_TIME <= '1';
			
		WHEN N12 =>
			DOOR_CLOSED <= '1';
			START_PROGRAM <= '1';
			DOOR_BLOCKED <= '1';
			EN_2SEC <= '1';
			EN_1MIN <= '1';
			EN1 <= '1';
			EN_TIME <= '1';
			
		WHEN N13 =>
			DOOR_CLOSED <= '1';
			START_PROGRAM <= '1';
			MESAJ <= '1';
			
	END CASE;

END PROCESS;

-- PROCESUL PENTRU STABILIREA STARII URMATOARE
PROCESS(STATE, CLOSE_OPEN_DOOR, START, T10, T20, T1, CAN_START, TEMPERATURE_REACHED, MANUAL_MODE)
BEGIN

	CASE STATE IS
		WHEN INITIAL_STATE =>
			NXT_STATE <= WAITING;
			
		WHEN WAITING =>
			IF MANUAL_MODE = '1' THEN
				NXT_STATE <= N1;
			ELSE
				NXT_STATE <= N2;
			END IF;
			
		WHEN N1 =>
			NXT_STATE <= N3;
			
		WHEN N2 =>
			NXT_STATE <= N3; 
			
		WHEN N3 =>
			IF CLOSE_OPEN_DOOR = '1' THEN
				NXT_STATE <= N4;
			ELSE
				NXT_STATE <= WAITING;
			END IF;
			
		WHEN N4 =>
			IF START = '1' AND CAN_START = '1' THEN
				NXT_STATE <= N5;
			ELSE
				NXT_STATE <= WAITING;
			END IF;

		WHEN N5 =>
			NXT_STATE <= N6;
			
		WHEN N6 =>
			IF PREWASH = '1' THEN
				NXT_STATE <= C1;
			ELSE NXT_STATE <= N7;
			END IF;
			
		WHEN C1 =>
			IF TEMPERATURE_REACHED = '1' THEN
				NXT_STATE <= C2;
			ELSE
				NXT_STATE <= C1;
			END IF;

		WHEN C2 =>
			NXT_STATE <= C3;

		WHEN C3 =>
			IF T10 = '1' THEN 
				NXT_STATE <= N7;
			ELSE
				NXT_STATE <= C3;
			END IF;

		WHEN N7 =>
			NXT_STATE <= C4;

		WHEN C4 =>
			IF TEMPERATURE_REACHED = '1' THEN
				NXT_STATE <= C5;
			ELSE
				NXT_STATE <= C4;
			END IF;

		WHEN C5 =>
			NXT_STATE <= C6;

		WHEN C6 =>
			IF T20 = '1' THEN 
				NXT_STATE <= N8;
			ELSE
				NXT_STATE <= C6;
			END IF;

		WHEN N8 =>
			NXT_STATE <= C7;

		WHEN C7 =>
			IF T10 = '1' THEN
				NXT_STATE <= N9;
			ELSE
				NXT_STATE <= C7;
			END IF;

		WHEN N9 =>
			IF ADDITIONAL_RINSE = '1' THEN
				NXT_STATE <= C8;
			ELSE
				NXT_STATE <= N10;
			END IF;

		WHEN C8 =>
			IF T10 = '1' THEN
				NXT_STATE <= N10;
			ELSE
				NXT_STATE <= C8;
			END IF;

		WHEN N10 =>
			NXT_STATE <= C9;

		WHEN C9 =>
			IF T10 = '1' THEN
				NXT_STATE <= N11;
			ELSE
				NXT_STATE <= C9;
			END IF;

		WHEN N11 =>
			NXT_STATE <= N12;

		WHEN N12 =>
			IF T1 = '1' THEN
				NXT_STATE <= N13;
			ELSE
				NXT_STATE <= N12;
			END IF;

		WHEN N13 =>
			IF CLOSE_OPEN_DOOR = '1' THEN
				NXT_STATE <= N13;
			ELSE
				NXT_STATE <= INITIAL_STATE;
			END IF;
			
	END CASE;
			
				

END PROCESS;

END TypeArchitecture;

// VHDL entity counter_1min, as the project stores it:
--STAN MIHAI ALEXANDRU
LIBRARY ieee;
USE ieee.std_logic_1164.all;
USE ieee.std_logic_unsigned.all;
ENTITY counter_1min IS
  PORT (
  	CLK_1MIN: IN STD_LOGIC;
  	EN_1MIN: IN STD_LOGIC;
  	T1: OUT STD_LOGIC
    );
END counter_1min;


ARCHITECTURE TypeArchitecture OF counter_1min IS

BEGIN

PROCESS(CLK_1MIN, EN_1MIN)
VARIABLE NR: STD_LOGIC := '0';
BEGIN

	IF EN_1MIN = '0' THEN
		NR := '0';
		T1 <= '0';
	ELSE 
		IF FALLING_EDGE(CLK_1MIN) THEN
			NR := not NR;
			IF NR = '1' THEN
				T1 <= '1';
				NR := '0';
			ELSE
				T1 <= '0';
			END IF;
		END IF;
	END IF;

END PROCESS;



END TypeArchitecture;

// VHDL entity MEMORIE_ROM, as the project stores it:
--TOSA CEZAR
LIBRARY ieee;
USE ieee.std_logic_1164.all;

ENTITY MEMORIE_ROM IS
  PORT (
  	PROGRAM_SELECTED: IN STD_LOGIC_VECTOR(2 DOWNTO 0);
  	PROGRAM_TEMPERATURE: OUT STD_LOGIC_VECTOR(3 DOWNTO 0);
  	PROGRAM_SPEED: OUT STD_LOGIC_VECTOR(2 DOWNTO 0);
  	PROGRAM_PREWASH: OUT STD_LOGIC;
  	PROGRAM_ADDITIONAL_RINSE: OUT STD_LOGIC
    );
END MEMORIE_ROM;


ARCHITECTURE TypeArchitecture OF MEMORIE_ROM IS

TYPE MEMORIE_ROM IS ARRAY(7 DOWNTO 0) OF STD_LOGIC_VECTOR(8 DOWNTO 0);
CONSTANT MEM: MEMORIE_ROM := ("000000000", "000000000", "000000000", "000100101",
						"010001010", "010001001", "001010000", "100000100");

SIGNAL MY_MEM: MEMORIE_ROM := ( OTHERS => "000000000");

SIGNAL SPEED_AUX: STD_LOGIC_VECTOR(3 DOWNTO 0);
SIGNAL CHARACTERISTICS: STD_LOGIC_VECTOR(8 DOWNTO 0) := (OTHERS => '0');
BEGIN

MY_MEM <= MEM;

PROCESS(PROGRAM_SELECTED)
BEGIN
	CASE PROGRAM_SELECTED IS
		WHEN "000" => CHARACTERISTICS <= MY_MEM(0);
		WHEN "001" => CHARACTERISTICS <= MY_MEM(1);
		WHEN "010" => CHARACTERISTICS <= MY_MEM(2);
		WHEN "011" => CHARACTERISTICS <= MY_MEM(3);
		WHEN "100" => CHARACTERISTICS <= MY_MEM(4);
		WHEN "101" => CHARACTERISTICS <= MY_MEM(5);
		WHEN "110" => CHARACTERISTICS <= MY_MEM(6);
		WHEN "111" => CHARACTERISTICS <= MY_MEM(7);
		WHEN OTHERS => CHARACTERISTICS <= (OTHERS => '0');
	END CASE;
END PROCESS;

PROGRAM_TEMPERATURE <= CHARACTERISTICS(8 DOWNTO 5);
PROGRAM_SPEED <= CHARACTERISTICS(4 DOWNTO 2);
PROGRAM_PREWASH <= CHARACTERISTICS(1);
PROGRAM_ADDITIONAL_RINSE <= CHARACTERISTICS(0); 

END TypeArchitecture;

// VHDL entity registru_1bit, as the project stores it:
--TOSA CEZAR
LIBRARY ieee;
USE ieee.std_logic_1164.all;

ENTITY registru_1bit IS
  PORT (
 	MODE: IN STD_LOGIC_VECTOR(1 DOWNTO 0);
	PL: IN STD_LOGIC;
	BTN, CLK: IN STD_LOGIC;
	Y: OUT STD_LOGIC
    );
END registru_1bit;

ARCHITECTURE TypeArchitecture OF registru_1bit IS

SIGNAL Y_AUX: STD_LOGIC := '0';

BEGIN

Y <= Y_AUX;

PROCESS(CLK)
VARIABLE WAS_ON: STD_LOGIC := '0';
BEGIN
	IF RISING_EDGE(CLK) THEN
		CASE MODE IS
			WHEN "00" => 
				IF BTN = '1' THEN
					WAS_ON := '1';
				ELSE
					NULL;
				END IF;
			WHEN "01" => 
				Y_AUX <= PL;
				WAS_ON := '0';
			WHEN "10" => 
				IF BTN = '0' AND WAS_ON = '1' THEN
					Y_AUX <= NOT Y_AUX;
					WAS_ON :='0';
				ELSE NULL;
				END IF;
				IF BTN = '1' THEN
					WAS_ON := '1';
				ELSE
					NULL;
				END IF;
			WHEN "11" => Y_AUX <= '0';
			WHEN OTHERS => Y_AUX <= '0';
		END CASE;
	END IF;
END PROCESS;

END TypeArchitecture;

// VHDL entity counter_time_left, as the project stores it:
--TOSA CEZAR
LIBRARY ieee;
USE ieee.std_logic_1164.all;
USE ieee.std_logic_unsigned.all;


ENTITY counter_time_left IS
  PORT (
  TOTAL_TIME: IN STD_LOGIC_VECTOR(6 DOWNTO 0);
  CLK_1MIN, EN_TIME: IN STD_LOGIC;
  LOAD: IN STD_LOGIC;
  TIME_LEFT: OUT STD_LOGIC_VECTOR(6 DOWNTO 0)
    );
END counter_time_left;


ARCHITECTURE TypeArchitecture OF counter_time_left IS

SIGNAL EN: STD_LOGIC := '0';

BEGIN

PROCESS(CLK_1MIN, EN_TIME, LOAD)
VARIABLE AUX: STD_LOGIC_VECTOR(6 DOWNTO 0) := (OTHERS => '0');
BEGIN
	IF EN_TIME = '0' THEN
		IF LOAD = '1' THEN
			AUX := TOTAL_TIME;
			TIME_LEFT <= TOTAL_TIME;
		ELSE
			NULL;
		END IF;
	ELSE
		IF FALLING_EDGE(CLK_1MIN) THEN
			IF AUX /= 0 THEN
				AUX := AUX - 1;
			ELSE
				NULL;
			END IF;
			TIME_LEFT <= AUX;
		END IF;
	END IF;
END PROCESS;
			

END TypeArchitecture;

// VHDL entity MUX_2_1_7BITS, as the project stores it:
-- STAN MIHAI ALEXANDRU
LIBRARY ieee;
USE ieee.std_logic_1164.all;

ENTITY MUX_2_1_7BITS IS
  PORT (
  	TOTAL_TIME, TIME_LEFT: IN STD_LOGIC_VECTOR(6 DOWNTO 0);
  	START_PROGRAM: IN STD_LOGIC;
  	TIME_FOR_SSD: OUT STD_LOGIC_VECTOR(6 DOWNTO 0)
    );
END MUX_2_1_7BITS;

--------------------------------------------------------------------------------
--Complete your VHDL description below
--------------------------------------------------------------------------------

ARCHITECTURE TypeArchitecture OF MUX_2_1_7BITS IS

BEGIN
with START_PROGRAM select TIME_FOR_SSD <=
TOTAL_TIME when '0',
TIME_LEFT when '1',
(OTHERS => '0') WHEN OTHERS;



END TypeArchitecture;

// VHDL entity calculate_total_time, as the project stores it:
-- STAN MIHAI ALEXANDRU
LIBRARY ieee;
USE ieee.std_logic_1164.all;
USE ieee.std_logic_unsigned.all;
ENTITY calculate_total_time IS
  PORT (
  	PREWASH, ADDITIONAL_RINSE: IN STD_LOGIC;
  	TEMPERATURE: IN STD_LOGIC_VECTOR(3 DOWNTO 0);
  	TOTAL_TIME: OUT STD_LOGIC_VECTOR(6 DOWNTO 0);
  	DELAY: OUT STD_LOGIC_VECTOR(5 DOWNTO 0)
    );
END calculate_total_time;

--------------------------------------------------------------------------------
--Complete your VHDL description below
--------------------------------------------------------------------------------

ARCHITECTURE TypeArchitecture OF calculate_total_time IS

BEGIN

--TOTAL_TIME <= AUX_TOTAL_TIME;
--DELAY <= AUX_DELAY;





PROCESS(PREWASH, ADDITIONAL_RINSE, TEMPERATURE)
VARIABLE AUX_TOTAL_TIME: STD_LOGIC_VECTOR(6 DOWNTO 0) := (OTHERS => '0');
VARIABLE AUX_DELAY: STD_LOGIC_VECTOR(5 DOWNTO 0) := (OTHERS => '0');
BEGIN
	AUX_TOTAL_TIME := (OTHERS => '0');
	AUX_TOTAL_TIME := AUX_TOTAL_TIME + 40;
	AUX_DELAY := (OTHERS => '0');
	IF PREWASH = '1' THEN
		AUX_TOTAL_TIME := AUX_TOTAL_TIME + 10;
	ELSE
		NULL;
	END IF;
	
	IF ADDITIONAL_RINSE = '1' THEN
		AUX_TOTAL_TIME := AUX_TOTAL_TIME + 10;
	ELSE
		NULL;
	END IF;

	CASE TEMPERATURE IS
		WHEN "0001" =>
			AUX_TOTAL_TIME := AUX_TOTAL_TIME + 2;
			AUX_DELAY := AUX_DELAY + 30;
			IF PREWASH = '1' THEN
				AUX_TOTAL_TIME := AUX_TOTAL_TIME + 3;
				AUX_DELAY := (OTHERS => '0');
			ELSE
				NULL;
			END IF;
			
		WHEN "0010" =>
			AUX_TOTAL_TIME := AUX_TOTAL_TIME + 1;
			AUX_DELAY := AUX_DELAY + 30;
			IF PREWASH = '1' THEN
				 AUX_TOTAL_TIME := AUX_TOTAL_TIME + 2;
				AUX_DELAY := (OTHERS => '0');
			ELSE
				NULL;
			END IF;
			
		WHEN "0100" =>
			AUX_DELAY := AUX_DELAY + 50;
			IF PREWASH = '1' THEN
				 AUX_TOTAL_TIME := AUX_TOTAL_TIME + 1;
				AUX_DELAY := AUX_DELAY - 10;
			ELSE
				NULL;
			END IF;
			
		WHEN "1000" =>
			AUX_DELAY := AUX_DELAY + 30;
			IF PREWASH = '1' THEN
				 AUX_TOTAL_TIME := AUX_TOTAL_TIME + 1;
				AUX_DELAY := (OTHERS => '0');
			ELSE
				NULL;
			END IF;
			
		WHEN OTHERS =>
			AUX_TOTAL_TIME := (OTHERS => '0');
			AUX_DELAY := (OTHERS => '0');
	END CASE;

	TOTAL_TIME <= AUX_TOTAL_TIME;
	DELAY <= AUX_DELAY;
	
END PROCESS;
	
END TypeArchitecture;

// VHDL entity calculate_temperature, as the project stores it:
--TOSA CEZAR
LIBRARY ieee;
USE ieee.std_logic_1164.all;
USE ieee.std_logic_unsigned.all;
ENTITY calculate_temperature IS
  PORT (
  	temp_mode: IN STD_LOGIC_VECTOR(3 DOWNTO 0);
  	TEMPERATURE: OUT STD_LOGIC_VECTOR(6 DOWNTO 0)
    );
END calculate_temperature;

--------------------------------------------------------------------------------
--Complete your VHDL description below
--------------------------------------------------------------------------------

ARCHITECTURE TypeArchitecture OF calculate_temperature IS
SIGNAL TEMP_AUX: STD_LOGIC_VECTOR(6 DOWNTO 0);
BEGIN
	WITH TEMP_MODE SELECT TEMPERATURE <=
			"0011110" WHEN "1000",
			"0101000" WHEN "0100",
			"0111100" WHEN "0010",
			"1011010" WHEN "0001",
			"0000000" WHEN OTHERS;
	

END TypeArchitecture;

// VHDL entity counter_delay, as the project stores it:
--TOSA CEZAR
LIBRARY ieee;
USE ieee.std_logic_1164.all;
USE ieee.std_logic_unsigned.all;
ENTITY counter_delay IS
  PORT (
  	EN: IN STD_LOGIC;
	CLK_2SEC: IN STD_LOGIC;
	DELAY: IN STD_LOGIC_VECTOR(5 DOWNTO 0);
	LOAD_DELAY: IN STD_LOGIC;
	Y: OUT STD_LOGIC
 );
END counter_delay;

ARCHITECTURE TypeArchitecture OF counter_delay IS

SIGNAL EN1: STD_LOGIC;

BEGIN

PROCESS(CLK_2SEC, EN, LOAD_DELAY)
VARIABLE AUX: STD_LOGIC_VECTOR(5 DOWNTO 0) := (OTHERS => '0');
BEGIN
	IF EN = '0' THEN
		IF LOAD_DELAY = '1' THEN
			AUX := DELAY;
			Y <= '0';
		ELSE
			NULL;
		END IF;
	ELSE
		IF DELAY = "000000" THEN
			Y <= '1';
		ELSE
			IF FALLING_EDGE(CLK_2SEC) THEN
				IF AUX /= 0 THEN
					AUX := AUX - 2;
				ELSE
					NULL;
				END IF;
				IF AUX = 0 THEN
					Y <=	'1';
				ELSE
					Y <= '0';
				END IF;
			END IF;
		END IF;
	END IF;
END PROCESS;
END TypeArchitecture;

// VHDL entity check_can_start, as the project stores it:
--TOSA CEZAR
LIBRARY ieee;
USE ieee.std_logic_1164.all;
USE ieee.std_logic_unsigned.all;


ENTITY check_can_start IS
  PORT (
 	TEMPERATURE: IN STD_LOGIC_VECTOR(3 DOWNTO 0);
 	SPEED: IN STD_LOGIC_VECTOR(2 DOWNTO 0);
 	CAN_START: OUT STD_LOGIC
    );
END check_can_start;

ARCHITECTURE TypeArchitecture OF check_can_start IS

BEGIN
PROCESS(TEMPERATURE, SPEED)
BEGIN	
	IF TEMPERATURE /= 0 AND SPEED /= 0 THEN
		CAN_START <= '1';
	ELSE
		CAN_START <= '0';
	END IF;
END PROCESS;

END TypeArchitecture;

// VHDL entity SSD_PROIECT, as the project stores it:
-- STAN MIHAI ALEXANDRU
library IEEE;
use IEEE.STD_LOGIC_1164.ALL;
use IEEE.STD_LOGIC_UNSIGNED.ALL;

entity SSD_PROIECT is
    port (
    		      Mesaj: in std_logic;
        input : in std_logic_vector(6 downto 0);
        CLK: in std_logic;
        anod: out std_logic_vector(3 downto 0);
        catod : out std_logic_vector(6 downto 0)
    );
end SSD_PROIECT;

architecture structural of SSD_PROIECT is

component convertor is
	port(
	number : in std_logic_vector(6 downto 0);
        d0,d1 : out std_logic_vector(3 downto 0)
    );
end component;


signal count : std_logic_vector(1 downto 0) := "00";
signal input_decoder: std_logic_vector(3 downto 0);
signal d0,d1,d2,d3: std_logic_vector(3 downto 0);

begin

	C1: convertor port map(input,d0,d1);
	d2 <= "0000";
	d3 <= "0000";
	process(clk)
	begin
	--if rising_edge(clk) then
	if rising_edge(clk) then 
		count<=count+1;
	end if;
	end process;

--Anozi
	process(count)
	begin
	case count is
	when "00" => anod <="0001";
	when "01" => anod <="0010";
	when "10" => anod <="0100";
	when "11" => anod <= "1000";
	when others => anod <="0000";
	end case;

	end process;

-- pentru digits
	process(count,d0,d1,d2,d3)
	BEGIN
	if Mesaj = '0' then
	case count is
	when "00" => input_decoder <= d1;
	when "01" => input_decoder <= d0;
	when "10" => input_decoder <= d2;
	when others => input_decoder <= d3;
	end case;
	else
		case count is
	when "00" => input_decoder <="0001";
	when "01" => input_decoder <="0010";
	when "10" => input_decoder <="0100";
	when "11" => input_decoder <= "1000";
	when others => input_decoder <="0000";
	end case;
	end if;
	end process;
	
	process(input_decoder)
	begin
	if Mesaj = '0' then
		case input_decoder is
		when "0000" => catod <= "0111111";  -- 0
        when "0001" => catod <= "0000110";  -- 1
        when "0010" => catod <= "1011011";  -- 2
        when "0011" => catod <= "1001111";  -- 3
        when "0100" => catod <= "1100110";  -- 4
        when "0101" => catod <= "1101101";  -- 5
        when "0110" => catod <= "1111101";  -- 6
        when "0111" => catod <= "0000111";  -- 7
        when "1000" => catod <= "1111111";  -- 8
        when "1001" => catod <= "1101111";  -- 9
        when others => catod <= "1111111";  -- default to all segments off
		end case;
	else 
		case input_decoder is
        when "0001" => catod <= "0000000";  
        when "0010" => catod <= "1011110";  
        when "0100" => catod <= "1010100";  
        when "1000" => catod <= "1111001";  
        when others => catod <= "1111111";  
        end case;
		end if;
		end process;
	
end structural;

library IEEE;
use IEEE.STD_LOGIC_1164.ALL;
use IEEE.NUMERIC_STD.ALL;
entity convertor is
    port (	
        number : in std_logic_vector(6 downto 0);
        d0,d1 : out std_logic_vector(3 downto 0)
    );
end entity;

architecture doamneee of convertor is
    signal ten : integer := 10;
    signal numar, digit1, digit2: INTEGER;
begin

    NUMAR <= to_integer(unsigned(number));
    digit1 <= NUMAR/ten;
    digit2 <= NUMAR MOD ten;
    d0 <= std_logic_vector(to_unsigned(digit1, d0'length));
    d1 <= std_logic_vector(to_unsigned(digit2, d1'length));

end architecture;

// VHDL entity Encoder, as the project stores it:
-- STAN MIHAI ALEXANDRU
LIBRARY ieee;
USE ieee.std_logic_1164.all;

ENTITY Encoder IS
  PORT (
 	A0: in std_logic;
 	A1: in std_logic;
 	A2: in std_logic;
 	A3: in std_logic;
 	A4: in std_logic;
 	ENCODED: out STD_logic_vector(2 downto 0)
    );
END Encoder;

--------------------------------------------------------------------------------
--Complete your VHDL description below
--------------------------------------------------------------------------------

ARCHITECTURE TypeArchitecture OF Encoder IS

BEGIN

	process(A0,A1,A2,A3,A4)
	BEGIN
	if A0 = '1' then
	ENCODED <= "000";
	elsif A1 = '1' then
	ENCODED <= "001";
	elsif A2 = '1' then
		ENCODED <= "010";
	elsif A3 = '1' then
		ENCODED <= "011";
	elsif A4 = '1' then
		ENCODED <= "100";
	else
		ENCODED <= "111";
	end if;
	end process;
END TypeArchitecture;

// VHDL entity divizor_frecventa_200Hz, as the project stores it:
-- STAN MIHAI ALEXANDRU
library IEEE;
use IEEE.STD_LOGIC_1164.ALL;

entity divizor_frecventa_200Hz is
    Port (
        clk_in : in  STD_LOGIC;
        clk_out: out STD_LOGIC
    );
end divizor_frecventa_200Hz;

architecture Behavioral of divizor_frecventa_200Hz is
    signal temporal: STD_LOGIC;
    signal counter : integer range 0 to 124999 := 0;
begin
    frequency_divider: process (clk_in) begin
        if rising_edge(clk_in) then
            if (counter = 124999) then
                temporal <= NOT(temporal);
                counter <= 0;
            else
                counter <= counter + 1;
            end if;
         end if;
    end process;
    
    clk_out <= temporal;
end Behavioral;

// VHDL entity debouncer_30ns, as the project stores it:
-- STAN MIHAI ALEXANDRU
LIBRARY ieee;
USE ieee.std_logic_1164.all;

ENTITY debouncer_30ns IS
  PORT (
  BTN, CLK_100MHZ: IN STD_LOGIC;
  BTN_DIS: OUT STD_LOGIC
    );
END debouncer_30ns;

ARCHITECTURE DEBOUNCER OF debouncer_30ns IS

COMPONENT bistabil IS
  PORT (
    CLK, D: IN STD_LOGIC;
    Q: OUT STD_LOGIC
    );
END COMPONENT;

SIGNAL Q0: STD_LOGIC := '0';
SIGNAL Q1: STD_LOGIC := '0';
SIGNAL Q2: STD_LOGIC := '0';
BEGIN

D3: bistabil PORT MAP(CLK_100MHZ, Q1, Q2);
D2: bistabil PORT MAP(CLK_100MHZ, Q0, Q1);
D1: bistabil PORT MAP(CLK_100MHZ, BTN, Q0);
BTN_DIS <= (Q0 AND Q1) AND Q2;

END DEBOUNCER;



LIBRARY ieee;
USE ieee.std_logic_1164.all;

ENTITY bistabil IS
  PORT (
    CLK, D: IN STD_LOGIC;
    Q: OUT STD_LOGIC
    );
END bistabil;

ARCHITECTURE comportamental OF bistabil IS

BEGIN

PROCESS(CLK)
BEGIN
    IF RISING_EDGE(CLK) THEN
        Q <= D;
    END IF;
END PROCESS;

END comportamental;

// VHDL entity Heater, as the project stores it:
-- STAN MIHAI ALEXANDRU


LIBRARY ieee;
USE ieee.std_logic_1164.all;
use ieee.std_logic_unsigned.all;

ENTITY Heater IS
  PORT (
	EN_WATER: in std_logic;
	CLK_2SEC: in std_logic;
	TEMP: in std_logic_vector(6 downto 0);
	TEMPERATURE: out std_logic
    );
END Heater;


ARCHITECTURE TypeArchitecture OF Heater IS
signal counter: std_logic_vector(6 downto 0) := "0001111";
BEGIN
	
process(EN_WATER,CLK_2SEC)
	BEGIN
	if EN_WATER = '0' then
		TEMPERATURE <= '0';
		counter <= "0001111";
	else
		
	if rising_edge(CLK_2SEC) and EN_WATER = '1' then
		counter <= counter + 1;
	if counter = TEMP then
		TEMPERATURE <= '1';
	else
		TEMPERATURE <= '0';
	end if;
	end if;	
	end if;	
	end process;

END TypeArchitecture;

// VHDL entity counter_10min, as the project stores it:
------------------------------------------------------------------
-- STAN MIHAI ALEXANDRU
LIBRARY ieee;
USE ieee.std_logic_1164.all;
use ieee.std_logic_unsigned.all;

ENTITY counter_10min IS
  PORT (
	CLK_1MIN: in std_logic;
  	EN10: in std_logic;
  	T10: out std_logic
    );
END counter_10min;

--------------------------------------------------------------------------------
--Complete your VHDL description below
--------------------------------------------------------------------------------

ARCHITECTURE TypeArchitecture OF counter_10min IS



BEGIN

	process(CLK_1MIN,EN10)
	variable counter: INTEGER := 0;
	BEGIN
	if EN10 = '0' then
		counter := 0;
		T10 <= '0';
	else
		if falling_edge(CLK_1MIN) then
			counter := counter + 1;
			if counter = 10 then
				counter := 0;
				T10 <= '1';
			else
				T10 <= '0';
			end if;
		end if;
	end if;
	end process;

END TypeArchitecture;

// VHDL entity counter_20min, as the project stores it:
------------------------------------------------------------------
-- STAN MIHAI ALEXANDRU
LIBRARY ieee;
USE ieee.std_logic_1164.all;
use ieee.std_logic_unsigned.all;

ENTITY counter_20min IS
  PORT (
	CLK_1MIN: in std_logic;
  	EN20: in std_logic;
  	T20: out std_logic
    );
END counter_20min;

--------------------------------------------------------------------------------
--Complete your VHDL description below
--------------------------------------------------------------------------------

ARCHITECTURE TypeArchitecture OF counter_20min IS



BEGIN

	process(CLK_1MIN,EN20)
	variable counter: INTEGER := 0;
	BEGIN
	if EN20 = '0' then
		counter := 0;
		T20 <= '0';
	else
		if falling_edge(CLK_1MIN) then
			counter := counter + 1;
			if counter = 20 then
				counter := 0;
				T20 <= '1';
			else
				T20 <= '0';
			end if;
		end if;
	end if;
	end process;

END TypeArchitecture;
